// Logisim project lab03_JK_DK_03124.circ as structural Verilog: 1 circuit, main circuit main
module main (
  input  in_1,
  input  in_2
);

  wire _0_2_q, _0_q, _0_qn, _1_2_q, _1_2_qn, _1_q, _1_qn, _2_2_q, _2_2_qn, _2_q, _2_qn, clock_1_out,
       clock_2_out, nand_1_out, nand_2_out, nor_1_out, nor_2_out, nor_3_out, nor_4_out, nor_5_out, not_1_out;

  Clock clock_1 (.out(clock_1_out));
  Clock clock_2 (.out(clock_2_out));
  J_K_Flip_Flop _2 (.J(nor_3_out), .clk(clock_1_out), .K(in_1), .Q(_2_q), .Qn(_2_qn));  // open: preset, en, reset
  D_Flip_Flop _2_2 (.clk(clock_2_out), .D(nor_1_out), .Q(_2_2_q), .Qn(_2_2_qn));  // open: preset, en, reset
  nor nor_1 (nor_1_out, _0_q, _1_qn);
  D_Flip_Flop _1 (.clk(clock_2_out), .D(nor_2_out), .Q(_1_q), .Qn(_1_qn));  // open: preset, en, reset
  nor nor_2 (nor_2_out, _1_q, _2_2_q);
  D_Flip_Flop _0 (.clk(clock_2_out), .D(nand_1_out), .Q(_0_q), .Qn(_0_qn));  // open: preset, en, reset
  nor nor_3 (nor_3_out, _1_2_qn, _0_2_q);
  J_K_Flip_Flop _1_2 (.J(_2_qn), .clk(clock_1_out), .K(in_2), .Q(_1_2_q), .Qn(_1_2_qn));  // open: preset, en, reset
  J_K_Flip_Flop _0_2 (.J(nor_4_out), .clk(clock_1_out), .K(_1_2_qn), .Q(_0_2_q));  // open: Qn, preset, en, reset
  nor nor_4 (nor_4_out, _1_2_q, _2_q);
  nand nand_1 (nand_1_out, nand_2_out, not_1_out);
  nand nand_2 (nand_2_out, _0_qn, _1_qn, _2_2_qn);
  LED _2_2_dup2 (.in(_2_q));
  LED _2_1 (.in(_1_2_q));
  LED _2_0 (.in(_0_2_q));
  LED led_1 (.in(_2_2_q));
  LED led_2 (.in(_1_q));
  LED led_3 (.in(_0_q));
  nor nor_5 (nor_5_out, _0_qn, _1_qn);
  not not_1 (not_1_out, nor_5_out);
endmodule
