// Logisim project lab04_JK_licznik_synch.circ as structural Verilog: 1 circuit, main circuit main
module main (
  input  in_1
);

  wire clock_1_out, j_k_ff_1_q, j_k_ff_1_qn, j_k_ff_2_q, j_k_ff_2_qn, j_k_ff_3_q, j_k_ff_4_q, nand_1_out,
       nor_1_out, not_1_out;

  Clock clock_1 (.out(clock_1_out));
  J_K_Flip_Flop #(.trigger("falling")) j_k_ff_1 (
    .J(j_k_ff_2_q), .clk(clock_1_out), .K(j_k_ff_2_q), .Q(j_k_ff_1_q), .Qn(j_k_ff_1_qn), .reset(in_1));  // open: preset, en
  J_K_Flip_Flop #(.trigger("falling")) j_k_ff_2 (
    .J(1'b1), .clk(clock_1_out), .K(1'b1), .Q(j_k_ff_2_q), .Qn(j_k_ff_2_qn), .reset(in_1));  // open: preset, en
  nor nor_1 (nor_1_out, j_k_ff_2_qn, j_k_ff_1_qn);
  J_K_Flip_Flop #(.trigger("falling")) j_k_ff_3 (
    .J(nor_1_out), .clk(clock_1_out), .K(nor_1_out), .Q(j_k_ff_3_q), .reset(in_1));  // open: Qn, preset, en
  J_K_Flip_Flop #(.trigger("falling")) j_k_ff_4 (
    .J(not_1_out), .clk(clock_1_out), .K(not_1_out), .Q(j_k_ff_4_q), .reset(in_1));  // open: Qn, preset, en
  not not_1 (not_1_out, nand_1_out);
  nand nand_1 (nand_1_out, j_k_ff_1_q, j_k_ff_2_q, j_k_ff_3_q);
  LED led_1 (.in(j_k_ff_1_q));
  LED led_2 (.in(j_k_ff_2_q));
  LED led_3 (.in(j_k_ff_3_q));
  LED led_4 (.in(j_k_ff_4_q));
endmodule
