// Logisim project lab04_licznik_mod6-10.circ as structural Verilog: 1 circuit, main circuit main
module main (
  input  in_1,
  input  in_2
);

  wire clock_1_out, clock_2_out, j_k_ff_1_q, j_k_ff_2_q, j_k_ff_3_q, j_k_ff_3_qn, j_k_ff_4_q, j_k_ff_5_q,
       j_k_ff_5_qn, j_k_ff_6_q, j_k_ff_6_qn, j_k_ff_7_q, j_k_ff_7_qn, j_k_ff_8_q, nor_1_out, nor_2_out,
       nor_3_out, nor_4_out, nor_5_out, nor_6_out, nor_7_out, nor_8_out, not_1_out, not_2_out, not_3_out,
       not_4_out, not_5_out, not_6_out, not_7_out, not_8_out, not_9_out, or_1_out;

  Clock clock_1 (.out(clock_1_out));
  Clock clock_2 (.out(clock_2_out));
  J_K_Flip_Flop #(.trigger("falling")) j_k_ff_1 (
    .J(1'b1), .clk(clock_1_out), .K(1'b1), .Q(j_k_ff_1_q), .reset(not_1_out));  // open: Qn, preset, en
  not not_1 (not_1_out, nor_1_out);
  J_K_Flip_Flop #(.trigger("falling")) j_k_ff_2 (
    .J(1'b1), .clk(clock_2_out), .K(1'b1), .Q(j_k_ff_2_q), .reset(not_2_out));  // open: Qn, preset, en
  not not_2 (not_2_out, or_1_out);
  J_K_Flip_Flop #(.trigger("falling")) j_k_ff_3 (
    .J(1'b1), .clk(j_k_ff_1_q), .K(1'b1), .Q(j_k_ff_3_q), .Qn(j_k_ff_3_qn), .reset(not_3_out));  // open: preset, en
  not not_3 (not_3_out, nor_1_out);
  not not_4 (not_4_out, or_1_out);
  J_K_Flip_Flop #(.trigger("falling")) j_k_ff_4 (
    .J(1'b1), .clk(j_k_ff_2_q), .K(1'b1), .Q(j_k_ff_4_q), .reset(not_4_out));  // open: Qn, preset, en
  J_K_Flip_Flop #(.trigger("falling")) j_k_ff_5 (
    .J(1'b1), .clk(j_k_ff_3_q), .K(1'b1), .Q(j_k_ff_5_q), .Qn(j_k_ff_5_qn), .reset(not_5_out));  // open: preset, en
  not not_5 (not_5_out, nor_1_out);
  J_K_Flip_Flop #(.trigger("falling")) j_k_ff_6 (
    .J(1'b1), .clk(j_k_ff_4_q), .K(1'b1), .Q(j_k_ff_6_q), .Qn(j_k_ff_6_qn), .reset(not_6_out));  // open: preset, en
  not not_6 (not_6_out, or_1_out);
  J_K_Flip_Flop #(.trigger("falling")) j_k_ff_7 (
    .J(1'b1), .clk(j_k_ff_5_q), .K(1'b1), .Q(j_k_ff_7_q), .Qn(j_k_ff_7_qn), .reset(not_7_out));  // open: preset, en
  not not_7 (not_7_out, nor_1_out);
  nor nor_1 (nor_1_out, nor_3_out, nor_8_out);
  J_K_Flip_Flop #(.trigger("falling")) j_k_ff_8 (
    .J(1'b1), .clk(j_k_ff_6_q), .K(1'b1), .Q(j_k_ff_8_q), .reset(not_8_out));  // open: Qn, preset, en
  not not_8 (not_8_out, or_1_out);
  or or_1 (or_1_out, nor_5_out, not_9_out);
  nor nor_2 (nor_2_out, j_k_ff_7_q, nor_6_out);
  nor nor_3 (nor_3_out, in_1, nor_2_out);
  nor nor_4 (nor_4_out, j_k_ff_6_qn, in_2);
  not not_9 (not_9_out, j_k_ff_4_q);
  nor nor_5 (nor_5_out, nor_4_out, j_k_ff_8_q);
  nor nor_6 (nor_6_out, j_k_ff_5_qn, j_k_ff_3_qn);
  nor nor_7 (nor_7_out, j_k_ff_3_q, j_k_ff_5_q);
  nor nor_8 (nor_8_out, j_k_ff_7_qn, nor_7_out);
  LED led_1 (.in(j_k_ff_8_q));
  LED led_2 (.in(j_k_ff_6_q));
  LED led_3 (.in(j_k_ff_4_q));
  LED led_4 (.in(j_k_ff_2_q));
  LED led_5 (.in(j_k_ff_7_q));
  LED led_6 (.in(j_k_ff_5_q));
  LED led_7 (.in(j_k_ff_3_q));
  LED led_8 (.in(j_k_ff_1_q));
endmodule
