// Logisim project lab01_NAND.circ as structural Verilog: 1 circuit, main circuit main
module main (
  input  in_1,
  input  in_2,
  input  in_3,
  input  in_4
);

  wire nand_1_out, nand_2_out, nand_3_out, nand_4_out, nand_5_out, not_1_out, not_2_out, not_3_out,
       not_4_out, not_5_out;

  not not_1 (not_1_out, in_1);
  not not_2 (not_2_out, in_2);
  not not_3 (not_3_out, in_3);
  nand nand_1 (nand_1_out, not_2_out, not_3_out);
  not not_4 (not_4_out, in_4);
  nand nand_2 (nand_2_out, not_1_out, in_4);
  nand nand_3 (nand_3_out, in_1, not_4_out);
  nand nand_4 (nand_4_out, nand_1_out, not_5_out);
  not not_5 (not_5_out, nand_3_out);
  nand nand_5 (nand_5_out, nand_2_out, nand_4_out);
  LED led_1 (.in(nand_5_out));
endmodule
