// Logisim project lab01_NOR.circ as structural Verilog: 1 circuit, main circuit main
module main (
  input  a,
  input  b,
  input  c,
  input  d
);

  wire nor_1_out, nor_2_out, nor_3_out, nor_4_out, nor_5_out, not_1_out, not_2_out, not_3_out, not_4_out;

  not not_1 (not_1_out, d);
  not not_2 (not_2_out, a);
  nor nor_1 (nor_1_out, b, c);
  nor nor_2 (nor_2_out, not_2_out, d);
  nor nor_3 (nor_3_out, a, not_1_out);
  not not_3 (not_3_out, nor_2_out);
  nor nor_4 (nor_4_out, nor_1_out, not_3_out);
  nor nor_5 (nor_5_out, nor_3_out, nor_4_out);
  LED led_1 (.in(not_4_out));
  not not_4 (not_4_out, nor_5_out);
endmodule
