// Logisim project lab02_sumator.circ as structural Verilog: 1 circuit, main circuit main
module main (
  input  a,
  input  b,
  input  c
);

  wire nor_1_out, nor_2_out, nor_3_out, nor_4_out, nor_5_out, nor_6_out, nor_7_out, nor_8_out, nor_9_out,
       not_1_out, not_2_out, not_3_out, not_4_out, not_5_out, not_6_out, not_7_out, not_8_out, not_9_out;

  not not_1 (not_1_out, a);
  not not_2 (not_2_out, b);
  not not_3 (not_3_out, a);
  not not_4 (not_4_out, b);
  nor nor_1 (nor_1_out, b, a);
  nor nor_2 (nor_2_out, not_1_out, not_2_out);
  nor nor_3 (nor_3_out, not_3_out, not_4_out);
  nor nor_4 (nor_4_out, nor_1_out, nor_2_out);
  not not_5 (not_5_out, nor_4_out);
  not not_6 (not_6_out, c);
  not not_7 (not_7_out, nor_4_out);
  not not_8 (not_8_out, c);
  nor nor_5 (nor_5_out, not_5_out, not_6_out);
  nor nor_6 (nor_6_out, nor_4_out, c);
  nor nor_7 (nor_7_out, not_7_out, not_8_out);
  nor nor_8 (nor_8_out, nor_5_out, nor_6_out);
  nor nor_9 (nor_9_out, nor_3_out, nor_7_out);
  LED S (.in(nor_8_out));
  not not_9 (not_9_out, nor_9_out);
  LED C_1 (.in(not_9_out));
endmodule
