// Logisim project lab02_transkoder_XOR.circ as structural Verilog: 1 circuit, main circuit main
module main (
  input  a,
  input  b,
  input  c
);

  wire xor_1_out, xor_2_out;

  xor xor_1 (xor_1_out, a, b);
  xor xor_2 (xor_2_out, b, c);
  LED w1 (.in(a));
  LED w2 (.in(xor_1_out));
  LED w3 (.in(xor_2_out));
endmodule
