// Logisim project lab05_JK_automat_mod4.circ as structural Verilog: 1 circuit, main circuit main
module main (
  input  in_1,
  input  in_2,
  output out_3,
  output out_4
);

  wire clock_1_out, j_k_ff_1_qn, not_1_out;

  Clock clock_1 (.out(clock_1_out));
  not not_1 (not_1_out, in_1);
  J_K_Flip_Flop #(.trigger("falling")) j_k_ff_1 (
    .J(in_1), .clk(clock_1_out), .K(not_1_out), .Q(out_4), .Qn(j_k_ff_1_qn), .reset(in_2));  // open: preset, en
  J_K_Flip_Flop #(.trigger("falling")) j_k_ff_2 (
    .J(out_4), .clk(clock_1_out), .K(j_k_ff_1_qn), .Q(out_3), .reset(in_2));  // open: Qn, preset, en
endmodule
